// Logisim project logism_Simulation.circ as structural Verilog: 10 circuits, main circuit ALU_ICG_Pipelined
// Data_in
module ALU (
  input  [15:0] in0,
  input  [15:0] in1,
  input  en0,
  input  en1,
  input  en2,
  input  en3,
  input  [5:0] opcode,
  output [3:0] flag,
  output [15:0] Data_out,
  output [15:0] xor0,
  output [15:0] xor1,
  output [15:0] xor2,
  output [15:0] xor3,
  output [15:0] xor4,
  output [15:0] xor5,
  output [15:0] xor6,
  output [15:0] xor7
);

  wire AU_1_c, AU_1_v, not_3_out;
  wire [15:0] multiplexer_2_out, not_1_out, not_2_out, Reg2_ff_out;

  assign not_1_out = ~in0;  // NOT_Gate not_1, 16 bits wide
  assign not_2_out = ~in1;  // NOT_Gate not_2, 16 bits wide
  Multiplexer #(.width(16)) multiplexer_1 (.in0(in0), .in1(not_1_out), .out(xor0), .sel(opcode[5]));
  Multiplexer #(.width(16)) multiplexer_2 (.in0(in1), .in1(not_2_out), .out(multiplexer_2_out), .sel(opcode[4]));
  Pipelining_register Reg1 (.FF_in(xor0), .clk(en0), .FF_out(xor1));
  Pipelining_register Reg2 (.FF_in(multiplexer_2_out), .clk(en0), .FF_out(Reg2_ff_out));
  AU AU_1 (.C_in(opcode[3]), .in0(xor1), .in1(Reg2_ff_out), .Output(xor2), .V(AU_1_v), .C(AU_1_c));
  LU LU_1 (.in0(xor1), .in1(Reg2_ff_out), .sel(opcode[3:1]), .out1(xor4));
  not not_3 (not_3_out, opcode[0]);
  Pipelining_register Reg3 (.FF_in(xor2), .clk(en1), .FF_out(xor3));
  Pipelining_register Reg4 (.FF_in(xor4), .clk(en2), .FF_out(xor5));
  and and_1 (flag[0], AU_1_v, not_3_out);
  and and_2 (flag[1], AU_1_c, not_3_out);
  Multiplexer #(.width(16)) multiplexer_3 (.in0(xor3), .in1(xor5), .out({flag[3], xor6[14:0]}), .sel(opcode[0]));
  nor nor_1 (flag[2], xor6[0], xor6[1], xor6[2], xor6[3], xor6[4], xor6[5], xor6[6], xor6[7], xor6[8], xor6[9], xor6[10], xor6[11], xor6[12], xor6[13], xor6[14], flag[3]);
  Pipelining_register Reg5 (.FF_in({flag[3], xor6[14:0]}), .clk(en3), .FF_out(Data_out));

  assign xor6[15] = flag[3];
  assign xor7 = Data_out;
endmodule

module AU (
  input  C_in,
  input  [15:0] in0,
  input  [15:0] in1,
  output [15:0] Output,
  output V,
  output C
);

  wire adder_1_cout, adder_2_cout, adder_3_cout, adder_4_cout, adder_5_cout, adder_6_cout, adder_7_cout,
       adder_8_cout, adder_9_cout, adder_10_cout, adder_11_cout, adder_12_cout, adder_13_cout, adder_14_cout,
       adder_15_cout;

  Adder #(.width(1)) adder_1 (.a(in0[0]), .b(in1[0]), .out(Output[0]), .cin(C_in), .cout(adder_1_cout));
  Adder #(.width(1)) adder_2 (.a(in0[1]), .b(in1[1]), .out(Output[1]), .cin(adder_1_cout), .cout(adder_2_cout));
  Adder #(.width(1)) adder_3 (.a(in0[2]), .b(in1[2]), .out(Output[2]), .cin(adder_2_cout), .cout(adder_3_cout));
  Adder #(.width(1)) adder_4 (.a(in0[3]), .b(in1[3]), .out(Output[3]), .cin(adder_3_cout), .cout(adder_4_cout));
  Adder #(.width(1)) adder_5 (.a(in0[4]), .b(in1[4]), .out(Output[4]), .cin(adder_4_cout), .cout(adder_5_cout));
  Adder #(.width(1)) adder_6 (.a(in0[5]), .b(in1[5]), .out(Output[5]), .cin(adder_5_cout), .cout(adder_6_cout));
  Adder #(.width(1)) adder_7 (.a(in0[6]), .b(in1[6]), .out(Output[6]), .cin(adder_6_cout), .cout(adder_7_cout));
  Adder #(.width(1)) adder_8 (.a(in0[7]), .b(in1[7]), .out(Output[7]), .cin(adder_7_cout), .cout(adder_8_cout));
  Adder #(.width(1)) adder_9 (.a(in0[8]), .b(in1[8]), .out(Output[8]), .cin(adder_8_cout), .cout(adder_9_cout));
  Adder #(.width(1)) adder_10 (.a(in0[9]), .b(in1[9]), .out(Output[9]), .cin(adder_9_cout), .cout(adder_10_cout));
  Adder #(.width(1)) adder_11 (.a(in0[10]), .b(in1[10]), .out(Output[10]), .cin(adder_10_cout), .cout(adder_11_cout));
  Adder #(.width(1)) adder_12 (.a(in0[11]), .b(in1[11]), .out(Output[11]), .cin(adder_11_cout), .cout(adder_12_cout));
  Adder #(.width(1)) adder_13 (.a(in0[12]), .b(in1[12]), .out(Output[12]), .cin(adder_12_cout), .cout(adder_13_cout));
  Adder #(.width(1)) adder_14 (.a(in0[13]), .b(in1[13]), .out(Output[13]), .cin(adder_13_cout), .cout(adder_14_cout));
  Adder #(.width(1)) adder_15 (.a(in0[14]), .b(in1[14]), .out(Output[14]), .cin(adder_14_cout), .cout(adder_15_cout));
  Adder #(.width(1)) adder_16 (.a(in0[15]), .b(in1[15]), .out(Output[15]), .cin(adder_15_cout), .cout(C));
  xor xor_1 (V, adder_15_cout, C);
endmodule

module LU (
  input  [15:0] in0,
  input  [15:0] in1,
  input  [2:0] sel,
  output [15:0] out1
);

  wire [15:0] and_1_out, not_1_out, not_2_out, or_1_out, xor_1_out;

  assign and_1_out = in0 & in1;  // AND_Gate and_1, 16 bits wide
  assign or_1_out = in0 | in1;  // OR_Gate or_1, 16 bits wide
  assign xor_1_out = in0 ^ in1;  // XOR_Gate xor_1, 16 bits wide
  assign not_1_out = ~and_1_out;  // NOT_Gate not_1, 16 bits wide
  assign not_2_out = ~or_1_out;  // NOT_Gate not_2, 16 bits wide
  Multiplexer #(.select(3), .width(16)) multiplexer_1 (
    .in0(in0), .in1(in1), .in2(and_1_out), .in3(not_1_out), .in4(or_1_out), .in5(not_2_out), .in6(xor_1_out),
    .out(out1), .sel(sel));  // open: in7
endmodule

module Binary_count (
  input  clk,
  output out0,
  output out1
);

  J_K_Flip_Flop j_k_ff_1 (.J(1'b1), .K(1'b1), .clk(clk), .Q(out0));  // open: Qn, preset, reset
  J_K_Flip_Flop j_k_ff_2 (.J(out0), .K(out0), .clk(clk), .Q(out1));  // open: Qn, preset, reset
endmodule

module Binary_decoder (
  input  in0,
  input  in1,
  output out0,
  output out1,
  output out2,
  output out3
);

  wire not_1_out, not_2_out;

  not not_1 (not_1_out, in0);
  not not_2 (not_2_out, in1);
  and and_1 (out0, not_1_out, not_2_out);
  and and_2 (out2, not_1_out, in1);
  and and_3 (out1, in0, not_2_out);
  and and_4 (out3, in1, in0);
endmodule

module ICG (
  input  en,
  input  [15:0] xor0,
  input  [15:0] xor1,
  input  clk,
  output ICG_out
);

  wire and_1_out, dlatch_1_q, or_1_out;
  wire [15:0] xor_1_out;

  assign xor_1_out = xor0 ^ xor1;  // XOR_Gate xor_1, 16 bits wide
  or or_1 (or_1_out, xor_1_out[0], xor_1_out[1], xor_1_out[2], xor_1_out[3], xor_1_out[4], xor_1_out[5], xor_1_out[6], xor_1_out[7], xor_1_out[8], xor_1_out[9], xor_1_out[10], xor_1_out[11], xor_1_out[12], xor_1_out[13], xor_1_out[14], xor_1_out[15]);
  and and_1 (and_1_out, or_1_out, en);
  DLatch dlatch_1 (.D(and_1_out), .en(clk), .Q(dlatch_1_q));
  and and_2 (ICG_out, dlatch_1_q, clk);
endmodule

module DLatch (
  input  D,
  input  en,
  output Q
);

  wire and_1_out, and_2_out, nor_2_out, not_1_out;

  not not_1 (not_1_out, D);
  and and_1 (and_1_out, not_1_out, en);
  and and_2 (and_2_out, en, D);
  nor nor_1 (Q, and_1_out, nor_2_out);
  nor nor_2 (nor_2_out, Q, and_2_out);
endmodule

module Pipelining_register (
  input  [15:0] FF_in,
  input  clk,
  output [15:0] FF_out
);

  D_Flip_Flop d_ff_1 (.D(FF_in[0]), .clk(clk), .Q(FF_out[0]));  // open: Qn, preset, reset
  D_Flip_Flop d_ff_2 (.D(FF_in[1]), .clk(clk), .Q(FF_out[1]));  // open: Qn, preset, reset
  D_Flip_Flop d_ff_3 (.D(FF_in[2]), .clk(clk), .Q(FF_out[2]));  // open: Qn, preset, reset
  D_Flip_Flop d_ff_4 (.D(FF_in[3]), .clk(clk), .Q(FF_out[3]));  // open: Qn, preset, reset
  D_Flip_Flop d_ff_5 (.D(FF_in[4]), .clk(clk), .Q(FF_out[4]));  // open: Qn, preset, reset
  D_Flip_Flop d_ff_6 (.D(FF_in[5]), .clk(clk), .Q(FF_out[5]));  // open: Qn, preset, reset
  D_Flip_Flop d_ff_7 (.D(FF_in[6]), .clk(clk), .Q(FF_out[6]));  // open: Qn, preset, reset
  D_Flip_Flop d_ff_8 (.D(FF_in[7]), .clk(clk), .Q(FF_out[7]));  // open: Qn, preset, reset
  D_Flip_Flop d_ff_9 (.D(FF_in[8]), .clk(clk), .Q(FF_out[8]));  // open: Qn, preset, reset
  D_Flip_Flop d_ff_10 (.D(FF_in[9]), .clk(clk), .Q(FF_out[9]));  // open: Qn, preset, reset
  D_Flip_Flop d_ff_11 (.D(FF_in[10]), .clk(clk), .Q(FF_out[10]));  // open: Qn, preset, reset
  D_Flip_Flop d_ff_12 (.D(FF_in[11]), .clk(clk), .Q(FF_out[11]));  // open: Qn, preset, reset
  D_Flip_Flop d_ff_13 (.D(FF_in[12]), .clk(clk), .Q(FF_out[12]));  // open: Qn, preset, reset
  D_Flip_Flop d_ff_14 (.D(FF_in[13]), .clk(clk), .Q(FF_out[13]));  // open: Qn, preset, reset
  D_Flip_Flop d_ff_15 (.D(FF_in[14]), .clk(clk), .Q(FF_out[14]));  // open: Qn, preset, reset
  D_Flip_Flop d_ff_16 (.D(FF_in[15]), .clk(clk), .Q(FF_out[15]));  // open: Qn, preset, reset
endmodule

module ALU_with_ICG (
  input  [15:0] A,
  input  [15:0] B,
  input  [5:0] OP_CODE,
  input  en0,
  input  en1,
  input  en2,
  input  en3,
  input  clk,
  output [3:0] flag_NZCV,
  output [15:0] ALU_out
);

  wire IGS0_icg_out, IGS1_icg_out, IGS2_icg_out, IGS3_icg_out;
  wire [15:0] ALU1_xor0, ALU1_xor1, ALU1_xor2, ALU1_xor3, ALU1_xor4, ALU1_xor5, ALU1_xor6, ALU1_xor7;

  ICG IGS1 (.en(en1), .xor0(ALU1_xor2), .xor1(ALU1_xor3), .clk(clk), .ICG_out(IGS1_icg_out));
  ICG IGS2 (.en(en2), .xor0(ALU1_xor4), .xor1(ALU1_xor5), .clk(clk), .ICG_out(IGS2_icg_out));
  ICG IGS0 (.en(en0), .xor0(ALU1_xor0), .xor1(ALU1_xor1), .clk(clk), .ICG_out(IGS0_icg_out));
  ICG IGS3 (.en(en3), .xor0(ALU1_xor6), .xor1(ALU1_xor7), .clk(clk), .ICG_out(IGS3_icg_out));
  ALU ALU1 (
    .in0(A), .in1(B), .en0(IGS0_icg_out), .en1(IGS1_icg_out), .en2(IGS2_icg_out), .en3(IGS3_icg_out),
    .opcode(OP_CODE), .flag(flag_NZCV), .Data_out(ALU_out), .xor0(ALU1_xor0), .xor1(ALU1_xor1),
    .xor2(ALU1_xor2), .xor3(ALU1_xor3), .xor4(ALU1_xor4), .xor5(ALU1_xor5), .xor6(ALU1_xor6), .xor7(ALU1_xor7));
endmodule

module ALU_ICG_Pipelined (
  input  [15:0] in0,
  input  [15:0] in1,
  input  [5:0] OP_CODE,
  output [3:0] flag_NZCV,
  output [15:0] ALU_out
);

  wire binary_count_1_out0, binary_count_1_out1, binary_decoder_1_out0, binary_decoder_1_out1,
       binary_decoder_1_out2, binary_decoder_1_out3, clock_1_out;

  Clock clock_1 (.out(clock_1_out));
  Binary_count binary_count_1 (.clk(clock_1_out), .out0(binary_count_1_out0), .out1(binary_count_1_out1));
  Binary_decoder binary_decoder_1 (
    .in0(binary_count_1_out0), .in1(binary_count_1_out1), .out0(binary_decoder_1_out0),
    .out1(binary_decoder_1_out1), .out2(binary_decoder_1_out2), .out3(binary_decoder_1_out3));
  ALU_with_ICG alu_with_icg_1 (
    .A(in0), .B(in1), .OP_CODE(OP_CODE), .en0(binary_decoder_1_out0), .en1(binary_decoder_1_out1),
    .en2(binary_decoder_1_out2), .en3(binary_decoder_1_out3), .clk(clock_1_out), .flag_NZCV(flag_NZCV),
    .ALU_out(ALU_out));
endmodule
